# Fritzing sketch esphome_ac (saved by Fritzing 0.9.4)
breadboards: 1

parts:
  WeMos_D1_Mini1 = WeMos D1 Mini
  Part3 = Adafruit AHT20 Temperature and Humidity Sensor [part_number="Adafruit #4566"]
  Mod1 = KY-005 Infrared Transmitter Module [package="Breakout board"]
  IR1 = TSOP312.., 314.. [package=THT]

nets:
  5V: WeMos_D1_Mini1.5V, Part3.VCC, Mod1.Vin, IR1.Vs
  N1: WeMos_D1_Mini1.D1, Part3.SCL
  N2: WeMos_D1_Mini1.D2, Part3.SDA
  N3: WeMos_D1_Mini1.D5, Mod1.S
  N4: WeMos_D1_Mini1.D6, IR1.Data
  GND: WeMos_D1_Mini1.G, Part3.GND, Mod1.-, IR1.GND

custom parts:
  Adafruit AHT20 Temperature and Humidity Sensor: The AHT20 is a nice but inexpensive temperature and humidity sensor from the same folks that brought us the DHT22. You can take sensor readings as often as you like, and it uses standard I2C so its super easy to use with any Arduino or Linux/Raspberry Pi board. This sensor has a typical accuracy of +- 2% relative humidity, and +-0.3 °C. There is only one I2C address so its not a good option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
  KY-005 Infrared Transmitter Module: Arduino IR Transmitter Module Keyes KY-005, emits infrared light at 38KHz.
