# Fritzing sketch probe-relayed (saved by Fritzing 0.9.4)
breadboards: 1

parts:
  WeMos_D1_Mini1 = WeMos D1 Mini
  eCO2+VOC = Adafruit CCS811 [part_number="Adafruit #3566"]
  Light = KY-018 Photoresistor Module [package="Breakout board"]
  DHT1 = DHT22 Humidity and Temperature Sensor
  WeMos_D1_Mini2 = WeMos D1 Mini
  Light1 = KY-018 Photoresistor Module [package="Breakout board"]
  DHT2 = DHT22 Humidity and Temperature Sensor
  Part2 = Adafruit BME680 [part_number="Adafruit #3660"]

nets:
  3V3: WeMos_D1_Mini1.3V3, DHT1.VDD
  N1: WeMos_D1_Mini1.A0, Light.S
  N2: WeMos_D1_Mini1.D0, Light.-
  N3: WeMos_D1_Mini1.D1, eCO2+VOC.SCL
  N4: WeMos_D1_Mini1.D2, eCO2+VOC.SDA
  N5: WeMos_D1_Mini1.D3, eCO2+VOC.3.3V
  N6: WeMos_D1_Mini1.D4, eCO2+VOC.GND
  N7: WeMos_D1_Mini1.D5, Light.Vin
  N8: WeMos_D1_Mini1.D6, eCO2+VOC.!WAKE
  N9: WeMos_D1_Mini1.D8, DHT1.DATA
  N10: WeMos_D1_Mini1.G, DHT1.GND
  3V3_2: WeMos_D1_Mini2.3V3, DHT2.VDD
  N11: WeMos_D1_Mini2.A0, Light1.S
  N12: WeMos_D1_Mini2.D0, Light1.-
  N13: WeMos_D1_Mini2.D1, Part2.SCK/SCL
  N14: WeMos_D1_Mini2.D2, Part2.SDI/SDA
  N15: WeMos_D1_Mini2.D3, Part2.3.3V
  N16: WeMos_D1_Mini2.D4, Part2.CS
  N17: WeMos_D1_Mini2.D5, Light1.Vin
  N18: WeMos_D1_Mini2.D6, Part2.GND
  N19: WeMos_D1_Mini2.D8, DHT2.DATA
  N20: WeMos_D1_Mini2.G, DHT2.GND

custom parts:
  Adafruit CCS811: Breathe easy - we finally have an I2C VOC/eCO2 sensor in the Adafruit shop! Add air quality monitoring to your project and with an Adafruit CCS811 Air Quality Sensor Breakout. This sensor from AMS is a gas sensor that can detect a wide range of Volatile Organic Compounds (VOCs) and is intended for indoor air quality monitoring. When connected to your microcontroller (running our library code)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
  KY-018 Photoresistor Module: KY-018 Photoresistor module, used to measure light intensity. It can determine the presence or absence of light.
