# Fritzing sketch probe-v3 (saved by Fritzing 0.9.4)
breadboards: 1

parts:
  eCO2+VOC = Adafruit CCS811 [part_number="Adafruit #3566"]  # not connected
  Light = KY-018 Photoresistor Module [package="Breakout board"]
  WeMos_D1_Mini2 = WeMos D1 Mini
  Part2 = Adafruit BME680 [part_number="Adafruit #3660"]
  TD-er1 = MH-Z19 CO2 sensor [part_number=MH-Z19]
  Part3 = Adafruit AHT20 Temperature and Humidity Sensor [part_number="Adafruit #4566"]  # not connected
  Part4 = Adafruit BME680 [part_number="Adafruit #3660"]  # not connected
  Mod1 = KY-005 Infrared Transmitter Module [package="Breakout board"]

nets:
  N1: Light.S, WeMos_D1_Mini2.A0
  VIN: Light.Vin, WeMos_D1_Mini2.3V3, Part2.3.3V
  GND: Light.-, WeMos_D1_Mini2.G, Part2.GND, TD-er1.GND, Mod1.-
  VIN_2: WeMos_D1_Mini2.5V, TD-er1.Vin, Mod1.Vin
  N2: WeMos_D1_Mini2.D0, Mod1.S
  N3: WeMos_D1_Mini2.D1, Part2.SCK/SCL
  N4: WeMos_D1_Mini2.D2, Part2.SDI/SDA
  N5: WeMos_D1_Mini2.RX, TD-er1.TX
  N6: WeMos_D1_Mini2.TX, TD-er1.RX

custom parts:
  Adafruit CCS811: Breathe easy - we finally have an I2C VOC/eCO2 sensor in the Adafruit shop! Add air quality monitoring to your project and with an Adafruit CCS811 Air Quality Sensor Breakout. This sensor from AMS is a gas sensor that can detect a wide range of Volatile Organic Compounds (VOCs) and is intended for indoor air quality monitoring. When connected to your microcontroller (running our library code)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
  KY-018 Photoresistor Module: KY-018 Photoresistor module, used to measure light intensity. It can determine the presence or absence of light.
  Adafruit AHT20 Temperature and Humidity Sensor: The AHT20 is a nice but inexpensive temperature and humidity sensor from the same folks that brought us the DHT22. You can take sensor readings as often as you like, and it uses standard I2C so its super easy to use with any Arduino or Linux/Raspberry Pi board. This sensor has a typical accuracy of +- 2% relative humidity, and +-0.3 °C. There is only one I2C address so its not a good option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
  KY-005 Infrared Transmitter Module: Arduino IR Transmitter Module Keyes KY-005, emits infrared light at 38KHz.
