# Fritzing sketch probe (saved by Fritzing 0.9.4)
breadboards: 1

parts:
  WeMos_D1_Mini1 = WeMos D1 Mini
  T+H+P = BME280 Breakout
  T+H+P+VOC = Adafruit BME680 [part_number="Adafruit #3660"]
  eCO2+VOC = Adafruit CCS811 [part_number="Adafruit #3566"]
  Light = KY-018 Photoresistor Module [package="Breakout board"]
  Adafruit_HUZZAH_ESP8266_Breakout1 = Adafruit HUZZAH ESP8266 Breakout [part_number=2471]  # not connected
  DHT1 = DHT22 Humidity and Temperature Sensor
  Movement = PIR sensor  # not connected

nets:
  3.3V: WeMos_D1_Mini1.3V3, T+H+P.3.3V, T+H+P.!CS, T+H+P+VOC.3.3V, T+H+P+VOC.CS, eCO2+VOC.3.3V, Light.Vin, DHT1.VDD
  N1: WeMos_D1_Mini1.A0, Light.S
  N2: WeMos_D1_Mini1.D1, eCO2+VOC.SCL
  N3: WeMos_D1_Mini1.D2, eCO2+VOC.SDA
  N4: WeMos_D1_Mini1.D3, T+H+P+VOC.SCK/SCL
  N5: WeMos_D1_Mini1.D4, T+H+P+VOC.SDI/SDA
  N6: WeMos_D1_Mini1.D5, T+H+P.SCK/SCL
  N7: WeMos_D1_Mini1.D6, T+H+P.SDI/SDA
  N8: WeMos_D1_Mini1.D8, DHT1.DATA
  GND: WeMos_D1_Mini1.G, T+H+P.GND, T+H+P.SDO/ADR, T+H+P+VOC.GND, T+H+P+VOC.SDO/ADR, eCO2+VOC.GND, eCO2+VOC.!WAKE, Light.-, DHT1.GND

custom parts:
  Adafruit CCS811: Breathe easy - we finally have an I2C VOC/eCO2 sensor in the Adafruit shop! Add air quality monitoring to your project and with an Adafruit CCS811 Air Quality Sensor Breakout. This sensor from AMS is a gas sensor that can detect a wide range of Volatile Organic Compounds (VOCs) and is intended for indoor air quality monitoring. When connected to your microcontroller (running our library code)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
  KY-018 Photoresistor Module: KY-018 Photoresistor module, used to measure light intensity. It can determine the presence or absence of light.
